# Fritzing sketch bosco_test_wOr8uHrcy7 (saved by Fritzing 0.9.3b)
circuit board: 8.46667cm x 5.64444cm
breadboards: 2

parts:
  Componente1 = Arduino Mega 2560 (Rev3)
  Componente2 = Bluetooth HC-05 Macho  # not connected
  R1 = PHOTOCELL [package=photocell-kit]
  Part1 = KY-008 Laser Transmitter Module [package="Breakout board"]
  R2 = Resistor [tolerance=±5% resistance=10k package="2010 [SMD]"]

nets:
  N1: Componente1.A0, R1.P$1, R2.Pin_1
  N2: Componente1.5V, R2.Pin_0
  N3: Componente1.GND, R1.P$2, Part1.-
  N4: Componente1.D2_PWM, Part1.S

custom parts:
  KY-008 Laser Transmitter Module: Laser Transmitter module KY-008 for Arduino, emits a dot shaped red laser beam.
